// Logisim project 16-bit_CPUimproved.circ as structural Verilog: 9 circuits, main circuit CPU
module CPU (
  output [15:0] out_1,
  output [5:0] out_2,
  output [15:0] out_3,
  output [15:0] out_4
);

  wire alu_1_out_5, ALUSrc, and_1_out, BEQ, clk, Jump, MemRead, MemToReg, MemWrite, RegDst, RegWrite;
  wire [1:0] ALUOp;
  wire [3:0] alu_control_1_operation;
  wire [4:0] instruction_decoder_1_rd_11_15, instruction_decoder_1_rs_21_25, instruction_decoder_1_rt_16_20,
       instruction_decoder_1_shamt_6_10, multiplexer_1_out;
  wire [5:0] instruction_decoder_1_funct_0_5;
  wire [15:0] adder_1_out, adder_2_out, data_memory_1_readdata, instruction_decoder_1_address_0_15,
       instruction_decoder_1_jump_15_0, multiplexer_2_out, multiplexer_3_out, program_counter_1_output,
       register_file_1_readdata1, register_file_1_readdata2;
  wire [31:0] instruction_memory_1_instruction;

  Program_Counter program_counter_1 (.\input (out_1), .\output (program_counter_1_output), .clk(clk));
  Clock clock_1 (.out(clk));
  Adder #(.width(16)) adder_1 (.a(16'h1), .b(program_counter_1_output), .out(adder_1_out));  // open: cin, cout
  Instruction_Memory instruction_memory_1 (
    .instruction(instruction_memory_1_instruction), .address(program_counter_1_output));
  Instruction_Decoder instruction_decoder_1 (
    .Instruction_code(instruction_memory_1_instruction), .address_0_15(instruction_decoder_1_address_0_15),
    .funct_0_5(instruction_decoder_1_funct_0_5), .shamt_6_10(instruction_decoder_1_shamt_6_10),
    .rd_11_15(instruction_decoder_1_rd_11_15), .rt_16_20(instruction_decoder_1_rt_16_20),
    .rs_21_25(instruction_decoder_1_rs_21_25), .opcode_26_31(out_2),
    .Jump_15_0(instruction_decoder_1_jump_15_0));
  Control_Unit control_unit_1 (
    .RegDst(RegDst), .ALUSrc(ALUSrc), .MemToReg(MemToReg), .RegWrite(RegWrite), .MemRead(MemRead),
    .MemWrite(MemWrite), .BEQ(BEQ), .opcode(out_2), .Jump(Jump), .aluOp(ALUOp));
  Multiplexer #(.width(5)) multiplexer_1 (
    .in0(instruction_decoder_1_rt_16_20), .in1(instruction_decoder_1_rd_11_15), .out(multiplexer_1_out),
    .sel(RegDst));  // open: en
  Register_File register_file_1 (
    .writeData(out_3), .ReadData1(register_file_1_readdata1), .readData2(register_file_1_readdata2),
    .addressBit(multiplexer_1_out), .readRegister2(instruction_decoder_1_rt_16_20),
    .readRegister1(instruction_decoder_1_rs_21_25), .Regwrite(RegWrite), .clk(clk));
  Multiplexer #(.width(16)) multiplexer_2 (
    .in0(register_file_1_readdata2), .in1(instruction_decoder_1_address_0_15), .out(multiplexer_2_out),
    .sel(ALUSrc));  // open: en
  ALU_Control alu_control_1 (
    .funct(instruction_decoder_1_funct_0_5), .operation(alu_control_1_operation), .ALUOp(ALUOp));
  Adder #(.width(16)) adder_2 (
    .a(adder_1_out), .b(instruction_decoder_1_address_0_15), .out(adder_2_out));  // open: cin, cout
  ALU alu_1 (
    .Rs_Data(register_file_1_readdata1), .Rt_Data(multiplexer_2_out), .AluOp(alu_control_1_operation),
    .shamt(instruction_decoder_1_shamt_6_10), .ALU_output(out_4), .out_5(alu_1_out_5));
  Multiplexer #(.width(16)) multiplexer_3 (
    .in0(adder_1_out), .in1(adder_2_out), .out(multiplexer_3_out), .sel(and_1_out));  // open: en
  and and_1 (and_1_out, BEQ, alu_1_out_5);
  Multiplexer #(.width(16)) multiplexer_4 (
    .in0(multiplexer_3_out), .in1(instruction_decoder_1_jump_15_0), .out(out_1), .sel(Jump));  // open: en
  Data_Memory data_memory_1 (
    .WriteData_2(MemWrite), .readData(data_memory_1_readdata), .readMemory(MemRead), .Address(out_4),
    .WriteData(register_file_1_readdata2), .clk(clk));
  Multiplexer #(.width(16)) multiplexer_5 (
    .in0(out_4), .in1(data_memory_1_readdata), .out(out_3), .sel(MemToReg));  // open: en
  Hex_Digit_Display hex_digit_display_1 (.value(out_3[11:8]));  // open: dp
  Hex_Digit_Display hex_digit_display_2 (.value(out_3[15:12]));  // open: dp
  Hex_Digit_Display hex_digit_display_3 (.value(out_3[3:0]));  // open: dp
  Hex_Digit_Display hex_digit_display_4 (.value(out_3[7:4]));  // open: dp

  // Notes on the sheet:
  //   System Clock
endmodule

module Register_File (
  input  [15:0] writeData,
  input  Regwrite,
  input  [4:0] readRegister1,
  input  [4:0] addressBit,
  input  [4:0] readRegister2,
  input  clk,
  output [15:0] ReadData1,
  output [15:0] readData2
);

  wire and_1_out, and_2_out, and_3_out, and_4_out, and_5_out, and_6_out, and_7_out, and_8_out, and_9_out,
       and_10_out, and_11_out, and_12_out, and_13_out, and_14_out, and_15_out, and_16_out, decoder_1_out0,
       decoder_1_out1, decoder_1_out2, decoder_1_out3, decoder_1_out4, decoder_1_out5, decoder_1_out6,
       decoder_1_out7, decoder_1_out8, decoder_1_out9, decoder_1_out10, decoder_1_out11, decoder_1_out12,
       decoder_1_out13, decoder_1_out14, decoder_1_out15;
  wire [15:0] register_1_q, register_2_q, register_3_q, register_4_q, register_5_q, register_6_q,
       register_7_q, register_8_q, register_9_q, register_10_q, register_11_q, register_12_q, register_13_q,
       register_14_q, register_15_q, register_16_q;

  Decoder #(.select(4)) decoder_1 (
    .out0(decoder_1_out0), .out1(decoder_1_out1), .out2(decoder_1_out2), .out3(decoder_1_out3),
    .out4(decoder_1_out4), .out5(decoder_1_out5), .out6(decoder_1_out6), .out7(decoder_1_out7),
    .out8(decoder_1_out8), .out9(decoder_1_out9), .out10(decoder_1_out10), .out11(decoder_1_out11),
    .out12(decoder_1_out12), .out13(decoder_1_out13), .out14(decoder_1_out14), .out15(decoder_1_out15),
    .sel(addressBit[3:0]));  // open: en
  and and_1 (and_1_out, Regwrite, decoder_1_out0);
  and and_2 (and_2_out, Regwrite, decoder_1_out1);
  and and_3 (and_3_out, Regwrite, decoder_1_out2);
  and and_4 (and_4_out, Regwrite, decoder_1_out3);
  and and_5 (and_5_out, Regwrite, decoder_1_out4);
  and and_6 (and_6_out, Regwrite, decoder_1_out5);
  and and_7 (and_7_out, Regwrite, decoder_1_out6);
  and and_8 (and_8_out, Regwrite, decoder_1_out7);
  and and_9 (and_9_out, Regwrite, decoder_1_out8);
  and and_10 (and_10_out, Regwrite, decoder_1_out9);
  and and_11 (and_11_out, Regwrite, decoder_1_out10);
  and and_12 (and_12_out, Regwrite, decoder_1_out11);
  and and_13 (and_13_out, Regwrite, decoder_1_out12);
  and and_14 (and_14_out, Regwrite, decoder_1_out13);
  and and_15 (and_15_out, Regwrite, decoder_1_out14);
  and and_16 (and_16_out, Regwrite, decoder_1_out15);
  Register #(.width(16)) register_1 (.D({16{1'b0}}), .en(and_1_out), .Q(register_1_q), .clk(clk));  // open: clr
  Register #(.width(16)) register_2 (.D(writeData), .en(and_2_out), .Q(register_2_q), .clk(clk));  // open: clr
  Register #(.width(16)) register_3 (.D(writeData), .en(and_3_out), .Q(register_3_q), .clk(clk));  // open: clr
  Register #(.width(16)) register_4 (.D(writeData), .en(and_4_out), .Q(register_4_q), .clk(clk));  // open: clr
  Register #(.width(16)) register_5 (.D(writeData), .en(and_5_out), .Q(register_5_q), .clk(clk));  // open: clr
  Register #(.width(16)) register_6 (.D(writeData), .en(and_6_out), .Q(register_6_q), .clk(clk));  // open: clr
  Register #(.width(16)) register_7 (.D(writeData), .en(and_7_out), .Q(register_7_q), .clk(clk));  // open: clr
  Register #(.width(16)) register_8 (.D(writeData), .en(and_8_out), .Q(register_8_q), .clk(clk));  // open: clr
  Register #(.width(16)) register_9 (.D(writeData), .en(and_9_out), .Q(register_9_q), .clk(clk));  // open: clr
  Register #(.width(16)) register_10 (.D(writeData), .en(and_10_out), .Q(register_10_q), .clk(clk));  // open: clr
  Register #(.width(16)) register_11 (.D(writeData), .en(and_11_out), .Q(register_11_q), .clk(clk));  // open: clr
  Register #(.width(16)) register_12 (.D(writeData), .en(and_12_out), .Q(register_12_q), .clk(clk));  // open: clr
  Register #(.width(16)) register_13 (.D(writeData), .en(and_13_out), .Q(register_13_q), .clk(clk));  // open: clr
  Register #(.width(16)) register_14 (.D(writeData), .en(and_14_out), .Q(register_14_q), .clk(clk));  // open: clr
  Register #(.width(16)) register_15 (.D(writeData), .en(and_15_out), .Q(register_15_q), .clk(clk));  // open: clr
  Register #(.width(16)) register_16 (.D(writeData), .en(and_16_out), .Q(register_16_q), .clk(clk));  // open: clr
  Multiplexer #(.select(4), .width(16)) multiplexer_1 (
    .in0(register_1_q), .in1(register_2_q), .in2(register_3_q), .in3(register_4_q), .in4(register_5_q),
    .in5(register_6_q), .in6(register_7_q), .in7(register_8_q), .in8(register_9_q), .in9(register_10_q),
    .in10(register_11_q), .in11(register_12_q), .in12(register_13_q), .in13(register_14_q),
    .in14(register_15_q), .in15(register_16_q), .out(ReadData1), .sel(readRegister1[3:0]));  // open: en
  Multiplexer #(.select(4), .width(16)) multiplexer_2 (
    .in0(register_1_q), .in1(register_2_q), .in2(register_3_q), .in3(register_4_q), .in4(register_5_q),
    .in5(register_6_q), .in6(register_7_q), .in7(register_8_q), .in8(register_9_q), .in9(register_10_q),
    .in10(register_11_q), .in11(register_12_q), .in12(register_13_q), .in13(register_14_q),
    .in14(register_15_q), .in15(register_16_q), .out(readData2), .sel(readRegister2[3:0]));  // open: en

  // Notes on the sheet:
  //   0
  //   1
  //   2
  //   3
  //   4
  //   5
  //   6
  //   7
  //   8
  //   9
  //   10
  //   11
  //   12
  //   13
  //   14
  //   15
endmodule

module ALU (
  input  [15:0] Rs_Data,
  input  [15:0] Rt_Data,
  input  [3:0] AluOp,
  input  [4:0] shamt,
  output out_5,
  output [15:0] ALU_output
);

  wire [15:0] adder_1_out, and_1_out, divider_1_out, multiplier_1_out, nor_1_out, or_1_out, shifter_1_out,
       shifter_2_out, subtractor_1_out, xor_1_out;

  Adder #(.width(16)) adder_1 (.a(Rs_Data), .b(Rt_Data), .out(adder_1_out));  // open: cin, cout
  Subtractor #(.width(16)) subtractor_1 (.a(Rs_Data), .b(Rt_Data), .out(subtractor_1_out));  // open: bin, bout
  Multiplier #(.width(16)) multiplier_1 (.a(Rs_Data), .b(Rt_Data), .out(multiplier_1_out));  // open: cin, cout
  Divider #(.width(16)) divider_1 (.a(Rs_Data), .b(Rt_Data), .out(divider_1_out));  // open: upper, rem
  assign or_1_out = Rs_Data | Rt_Data;  // OR_Gate or_1, 16 bits wide
  assign and_1_out = Rs_Data & Rt_Data;  // AND_Gate and_1, 16 bits wide
  assign xor_1_out = Rs_Data ^ Rt_Data;  // XOR_Gate xor_1, 16 bits wide
  assign nor_1_out = ~(Rs_Data | Rt_Data);  // NOR_Gate nor_1, 16 bits wide
  Shifter #(.width(16)) shifter_1 (.in(Rs_Data), .\dist (shamt[3:0]), .out(shifter_1_out));
  Shifter #(.width(16), .shift("lr")) shifter_2 (.in(Rs_Data), .\dist (shamt[3:0]), .out(shifter_2_out));
  Multiplexer #(.select(4), .width(16)) multiplexer_1 (
    .in0(adder_1_out), .in1(subtractor_1_out), .in2(or_1_out), .in3(and_1_out), .in4(xor_1_out),
    .in5(nor_1_out), .in6(multiplier_1_out), .in7(divider_1_out), .in8(shifter_1_out), .in9(shifter_2_out),
    .out(ALU_output), .sel(AluOp));  // open: in10, in11, in12, in13, in14, in15, en
  nor nor_2 (out_5, ALU_output[0], ALU_output[1], ALU_output[2], ALU_output[3], ALU_output[4], ALU_output[5], ALU_output[6], ALU_output[7], ALU_output[9], ALU_output[10], ALU_output[11], ALU_output[12], ALU_output[13], ALU_output[14], ALU_output[15], ALU_output[8]);
endmodule

module Control_Unit (
  input  [5:0] opcode,
  output RegDst,
  output ALUSrc,
  output MemToReg,
  output RegWrite,
  output MemRead,
  output MemWrite,
  output BEQ,
  output [1:0] aluOp,
  output Jump
);

  wire ADDI_out;

  and R_Type (aluOp[1], ~opcode[5], ~opcode[4], ~opcode[3], ~opcode[2], ~opcode[1], ~opcode[0]);  // AND_Gate
  and ADDI (ADDI_out, ~opcode[5], ~opcode[4], opcode[3], ~opcode[2], ~opcode[1], ~opcode[0]);  // AND_Gate
  and LW (MemRead, opcode[5], ~opcode[4], ~opcode[3], ~opcode[2], opcode[1], opcode[0]);  // AND_Gate
  and SW (MemWrite, opcode[5], ~opcode[4], opcode[3], ~opcode[2], opcode[1], opcode[0]);  // AND_Gate
  and u_BEQ (aluOp[0], ~opcode[5], ~opcode[4], ~opcode[3], opcode[2], ~opcode[1], ~opcode[0]);  // AND_Gate
  or or_1 (ALUSrc, MemRead, ADDI_out, MemWrite);
  or or_2 (RegWrite, aluOp[1], ADDI_out, MemRead);
  and J (Jump, ~opcode[5], ~opcode[4], ~opcode[3], ~opcode[2], opcode[1], ~opcode[0]);  // AND_Gate

  assign BEQ = aluOp[0];
  assign MemToReg = MemRead;
  assign RegDst = aluOp[1];
endmodule

module Instruction_Memory (
  input  [15:0] address,
  output [31:0] instruction
);

  ROM #(.addrWidth(16), .dataWidth(32)) rom_1 (.addr(address), .data(instruction));  // open: sel
endmodule

module Data_Memory (
  input  [15:0] Address,
  input  [15:0] WriteData,
  input  clk,
  input  readMemory,
  input  WriteData_2,
  output [15:0] readData
);

  RAM #(.addrWidth(16), .dataWidth(16), .bus("separate")) ram_1 (
    .addr(Address), .din(WriteData), .data(readData), .str(WriteData_2), .clk(clk), .ld(readMemory));  // open: sel, clr
endmodule

module Program_Counter (
  input  [15:0] \input ,
  input  clk,
  output [15:0] \output 
);

  Register #(.width(16)) register_1 (.D(\input ), .en(1'b1), .Q(\output ), .clk(clk));  // open: clr
endmodule

module ALU_Control (
  input  [5:0] funct,
  input  [1:0] ALUOp,
  output [3:0] operation
);

  wire ADD_out, and_1_out, AND_2_out, DIV_out, MUL_out, NOR_out, not_1_out, not_2_out, or_2_out, or_3_out,
       OR_out, SUB_out, XOR_out;

  not not_1 (not_1_out, ALUOp[0]);
  not not_2 (not_2_out, ALUOp[1]);
  and and_1 (and_1_out, not_2_out, ALUOp[0]);
  and ADD (ADD_out, ~funct[3], ~funct[2], ~funct[1], ~funct[0]);  // AND_Gate
  and SUB (SUB_out, ~funct[3], ~funct[2], funct[1], ~funct[0]);  // AND_Gate
  and OR (OR_out, ~funct[3], funct[2], ~funct[1], funct[0]);  // AND_Gate
  and AND_2 (AND_2_out, ~funct[3], funct[2], ~funct[1], ~funct[0]);  // AND_Gate
  and XOR (XOR_out, ~funct[3], funct[2], funct[1], ~funct[0]);  // AND_Gate
  and NOR (NOR_out, ~funct[3], funct[2], funct[1], funct[0]);  // AND_Gate
  and MUL (MUL_out, funct[4], funct[3], ~funct[2], ~funct[1], ~funct[0]);  // AND_Gate
  and DIV (DIV_out, funct[4], funct[3], ~funct[2], funct[1], ~funct[0]);  // AND_Gate
  or or_2 (or_2_out, ADD_out, not_1_out);
  or or_3 (or_3_out, and_1_out, XOR_out);
  Priority_Encoder #(.select(4)) priority_encoder_1 (
    .in0(or_2_out), .in1(SUB_out), .in2(OR_out), .in3(AND_2_out), .in4(or_3_out), .in5(NOR_out),
    .in6(MUL_out), .in7(DIV_out), .out(operation));  // open: in8, in9, in10, in11, in12, in13, in14, in15, gs, en_out, en_in
endmodule

module Instruction_Decoder (
  input  [31:0] Instruction_code,
  output [15:0] Jump_15_0,
  output [15:0] address_0_15,
  output [5:0] funct_0_5,
  output [4:0] shamt_6_10,
  output [4:0] rd_11_15,
  output [4:0] rt_16_20,
  output [4:0] rs_21_25,
  output [5:0] opcode_26_31
);


  assign address_0_15 = Instruction_code[15:0];
  assign funct_0_5 = Instruction_code[5:0];
  assign Jump_15_0 = Instruction_code[15:0];
  assign opcode_26_31 = Instruction_code[31:26];
  assign rd_11_15 = Instruction_code[15:11];
  assign rs_21_25 = Instruction_code[25:21];
  assign rt_16_20 = Instruction_code[20:16];
  assign shamt_6_10 = Instruction_code[10:6];
endmodule
